# Fritzing sketch Luxmetro (saved by Fritzing 0.9.3b)

parts:
  WeMos_D1_Mini1 = WeMos D1 Mini
  WeMos_D1_Mini_OLED_Shield1 = WeMos D1 Mini OLED Shield

nets:
  3V3: WeMos_D1_Mini1.3V3, WeMos_D1_Mini_OLED_Shield1.3V3

notes:
  MAX44009
  VIN = rosso
  GND = nero
  SCL = giallo
  SDA = verde
